// Digital circuit 8bitReg.dig as structural Verilog
module _8bitReg (
  input  Clock,
  input  [7:0] Data,
  input  bLoad,
  input  bOE,
  output [7:0] RegState,
  output [7:0] BusOut
);

  _74173 _74173_1 (
    .pin1(1'b0), .pin2(1'b0), .pin3(RegState[3]), .pin4(RegState[2]), .pin5(RegState[1]), .pin6(RegState[0]),
    .pin7(Clock), .pin8(1'b0), .pin9(bLoad), .pin10(bLoad), .pin11(Data[0]), .pin12(Data[1]),
    .pin13(Data[2]), .pin14(Data[3]), .pin15(1'b0), .pin16(1'b1));
  _74173 _74173_2 (
    .pin1(1'b0), .pin2(1'b0), .pin3(RegState[7]), .pin4(RegState[6]), .pin5(RegState[5]), .pin6(RegState[4]),
    .pin7(Clock), .pin8(1'b0), .pin9(bLoad), .pin10(bLoad), .pin11(Data[4]), .pin12(Data[5]),
    .pin13(Data[6]), .pin14(Data[7]), .pin15(1'b0), .pin16(1'b1));
  _74245 _74245_1 (
    .pin1(1'b1), .pin2(RegState[0]), .pin3(RegState[1]), .pin4(RegState[2]), .pin5(RegState[3]),
    .pin6(RegState[4]), .pin7(RegState[5]), .pin8(RegState[6]), .pin9(RegState[7]), .pin10(1'b0),
    .pin11(BusOut[7]), .pin12(BusOut[6]), .pin13(BusOut[5]), .pin14(BusOut[4]), .pin15(BusOut[3]),
    .pin16(BusOut[2]), .pin17(BusOut[1]), .pin18(BusOut[0]), .pin19(bOE), .pin20(1'b1));
endmodule
