// Digital circuit Alu.dig as structural Verilog
module Alu (
  input  [7:0] A,
  input  [7:0] B,
  input  Subtract,
  input  bOE,
  output Carry,
  output [7:0] AluStatus,
  output [7:0] AluOut
);

  wire _7486_1_pin3, _7486_1_pin6, _7486_1_pin8, _7486_1_pin11, _7486_2_pin3, _7486_2_pin6, _7486_2_pin8,
       _7486_2_pin11, _74283_1_pin9;

  _7486 _7486_1 (
    .pin1(B[0]), .pin2(Subtract), .pin3(_7486_1_pin3), .pin4(B[1]), .pin5(Subtract), .pin6(_7486_1_pin6),
    .pin7(1'b0), .pin8(_7486_1_pin8), .pin9(B[2]), .pin10(Subtract), .pin11(_7486_1_pin11), .pin12(B[3]),
    .pin13(Subtract), .pin14(1'b1));
  _7486 _7486_2 (
    .pin1(B[4]), .pin2(Subtract), .pin3(_7486_2_pin3), .pin4(B[5]), .pin5(Subtract), .pin6(_7486_2_pin6),
    .pin7(1'b0), .pin8(_7486_2_pin8), .pin9(B[6]), .pin10(Subtract), .pin11(_7486_2_pin11), .pin12(B[7]),
    .pin13(Subtract), .pin14(1'b1));
  _74283 _74283_1 (
    .pin1(AluStatus[1]), .pin2(_7486_1_pin6), .pin3(A[1]), .pin4(AluStatus[0]), .pin5(A[0]),
    .pin6(_7486_1_pin3), .pin7(Subtract), .pin8(1'b0), .pin9(_74283_1_pin9), .pin10(AluStatus[3]),
    .pin11(_7486_1_pin11), .pin12(A[3]), .pin13(AluStatus[2]), .pin14(A[2]), .pin15(_7486_1_pin8),
    .pin16(1'b1));
  _74283 _74283_2 (
    .pin1(AluStatus[5]), .pin2(_7486_2_pin6), .pin3(A[5]), .pin4(AluStatus[4]), .pin5(A[4]),
    .pin6(_7486_2_pin3), .pin7(_74283_1_pin9), .pin8(1'b0), .pin9(Carry), .pin10(AluStatus[7]),
    .pin11(_7486_2_pin11), .pin12(A[7]), .pin13(AluStatus[6]), .pin14(A[6]), .pin15(_7486_2_pin8),
    .pin16(1'b1));
  _74245 _74245_1 (
    .pin1(1'b0), .pin2(AluOut[7]), .pin3(AluOut[6]), .pin4(AluOut[5]), .pin5(AluOut[4]), .pin6(AluOut[3]),
    .pin7(AluOut[2]), .pin8(AluOut[1]), .pin9(AluOut[0]), .pin10(1'b0), .pin11(AluStatus[0]),
    .pin12(AluStatus[1]), .pin13(AluStatus[2]), .pin14(AluStatus[3]), .pin15(AluStatus[4]),
    .pin16(AluStatus[5]), .pin17(AluStatus[6]), .pin18(AluStatus[7]), .pin19(bOE), .pin20(1'b1));
endmodule
