// Digital circuit Clock.dig as structural Verilog
module Clock (
  input  Clock,
  input  Manual,
  input  Toggle,
  output Output
);

  wire and_1_out, and_2_out, not_1_out;

  not not_1 (not_1_out, Toggle);
  and and_1 (and_1_out, Clock, Toggle);
  and and_2 (and_2_out, not_1_out, Manual);
  or or_1 (Output, and_1_out, and_2_out);
endmodule
