// Digital circuit main.dig as structural Verilog
module main (
  input  clk,
  input  [7:0] BusData,
  input  bLoad_A,
  input  bOE_A,
  input  Subtract,
  input  bOE_ALU
);

  wire alu_1_carry, button_1_out, clock_1_output, dipswitch_1_out;
  wire [7:0] A_Reg_busout, A_Reg_regstate, alu_1_alustatus, undriven;

  Button button_1 (.out(button_1_out));
  DipSwitch dipswitch_1 (.out(dipswitch_1_out));
  Clock clock_1 (.Clock(clk), .Manual(button_1_out), .Toggle(dipswitch_1_out), .Output(clock_1_output));
  LED led_1 (.in(A_Reg_regstate[7]));
  _8bitReg A_Reg (
    .Clock(clock_1_output), .Data(A_Reg_busout), .bLoad(bLoad_A), .bOE(bOE_A), .RegState(A_Reg_regstate),
    .BusOut(A_Reg_busout));
  LED led_2 (.in(alu_1_carry));
  Alu alu_1 (
    .A(A_Reg_regstate), .B(undriven), .Subtract(Subtract), .bOE(bOE_ALU), .Carry(alu_1_carry),
    .AluStatus(alu_1_alustatus), .AluOut(A_Reg_busout));
  LED led_3 (.in(A_Reg_regstate[6]));
  LED led_4 (.in(A_Reg_regstate[5]));
  LED led_5 (.in(alu_1_alustatus[7]));
  LED led_6 (.in(alu_1_alustatus[6]));
  LED led_7 (.in(A_Reg_regstate[4]));
  LED led_8 (.in(A_Reg_regstate[3]));
  LED led_9 (.in(alu_1_alustatus[5]));
  LED led_10 (.in(alu_1_alustatus[4]));
  LED led_11 (.in(A_Reg_regstate[2]));
  LED led_12 (.in(A_Reg_regstate[1]));
  LED led_13 (.in(alu_1_alustatus[3]));
  LED led_14 (.in(alu_1_alustatus[2]));
  LED led_15 (.in(A_Reg_regstate[0]));
  LED led_16 (.in(alu_1_alustatus[1]));
  LED led_17 (.in(alu_1_alustatus[0]));
  LED led_18 (.in(A_Reg_busout[7]));
  LED led_19 (.in(A_Reg_busout[6]));
  LED led_20 (.in(A_Reg_busout[5]));
  LED led_21 (.in(A_Reg_busout[4]));
  Switch #(.Bits(8)) switch_1 (.A(BusData), .B(A_Reg_busout));
  LED led_22 (.in(A_Reg_busout[3]));
  LED led_23 (.in(A_Reg_busout[2]));
  LED led_24 (.in(A_Reg_busout[1]));
  LED led_25 (.in(A_Reg_busout[0]));

  // Notes on the sheet:
  //   bLoad_A: default 1
  //   bOE_A: default 1
  //   bOE_ALU: default 1
  //   DATA BUS
endmodule
